# Fritzing sketch barebones-arduino_Arduino-no-FTDI (saved by Fritzing 0.9.1b)
circuit board: 6.49111cm x 4.61366cm
breadboards: 1

parts:
  S1 = Pushbutton [package="[THT]"]
  XTAL1 = Crystal [frequency="16 Mhz" package=THT]
  C4 = Ceramic Capacitor [capacitance=100nF package="200 mil [THT, multilayer]"]
  R1 = Resistor [tolerance=±5% resistance=1k package=THT]
  C3 = Ceramic Capacitor [capacitance=100nF package="200 mil [THT, multilayer]"]
  U2 = atmega328 [package=dip]

nets (from the breadboard view):
  N1: S1.Pin_1, S1.Pin_2, R1.Pin_1, U2.RESET
  N2: S1.Pin_3, S1.Pin_4, C4.1, C3.1, U2.GND
  N3: XTAL1.pin_0, C3.0, U2.XLAT1
  N4: XTAL1.pin_1, C4.0, U2.XLAT2
  N5: R1.Pin_0, U2.VCC, U2.AVCC
