# Fritzing sketch make_your_own_uno (saved by Fritzing 0.8.7b)
breadboards: 1

parts:
  U1 = atmega328 [package=dip]
  S1 = Pushbutton [package="[THT]"]
  Part1 = Arduino Uno (Rev3)
  C1 = Ceramic Capacitor [capacitance=10pF package="100 mil [THT, multilayer]"]
  C2 = Ceramic Capacitor [capacitance=10pF package="100 mil [THT, multilayer]"]
  XTAL1 = Crystal [frequency="16 Mhz" package=THT]
  R1 = Resistor [tolerance=±5% resistance=10k package=THT]

nets:
  N1: U1.RESET, S1.Pin_1, S1.Pin_2, Part1.RESET, R1.Pin_1
  N2: U1.D0_(RX), Part1.D0/RX
  N3: U1.D1_(TX), Part1.D1/TX
  N4: U1.XLAT1, C1.0, XTAL1.pin_0
  N5: U1.XLAT2, C2.0, XTAL1.pin_1
  N6: U1.AVCC, U1.AREF, Part1.5V, R1.Pin_0
  N7: U1.GND#21, S1.Pin_3, S1.Pin_4, Part1.GND, C1.1, C2.1
